// Logisim project alu.circ as structural Verilog
module L_16_bit_NOT (
  input  [15:0] I,
  output [15:0] O
);

  not not_1 (O[15], I[15]);
  not not_2 (O[14], I[14]);
  not not_3 (O[13], I[13]);
  not not_4 (O[12], I[12]);
  not not_5 (O[11], I[11]);
  not not_6 (O[10], I[10]);
  not not_7 (O[9], I[9]);
  not not_8 (O[8], I[8]);
  not not_9 (O[7], I[7]);
  not not_10 (O[6], I[6]);
  not not_11 (O[5], I[5]);
  not not_12 (O[4], I[4]);
  not not_13 (O[3], I[3]);
  not not_14 (O[2], I[2]);
  not not_15 (O[1], I[1]);
  not not_16 (O[0], I[0]);
endmodule

module L_16_bit_AND (
  input  [15:0] A,
  input  [15:0] B,
  output [15:0] O
);

  and and_1 (O[15], A[15], B[15]);
  and and_2 (O[14], A[14], B[14]);
  and and_3 (O[13], A[13], B[13]);
  and and_4 (O[12], A[12], B[12]);
  and and_5 (O[11], A[11], B[11]);
  and and_6 (O[10], A[10], B[10]);
  and and_7 (O[9], A[9], B[9]);
  and and_8 (O[8], A[8], B[8]);
  and and_9 (O[7], A[7], B[7]);
  and and_10 (O[6], A[6], B[6]);
  and and_11 (O[5], A[5], B[5]);
  and and_12 (O[4], A[4], B[4]);
  and and_13 (O[3], A[3], B[3]);
  and and_14 (O[2], A[2], B[2]);
  and and_15 (O[1], A[1], B[1]);
  and and_16 (O[0], A[0], B[0]);
endmodule

module L_16_bit_OR (
  input  [15:0] A,
  input  [15:0] B,
  output [15:0] O
);

  or or_1 (O[15], A[15], B[15]);
  or or_2 (O[14], A[14], B[14]);
  or or_3 (O[13], A[13], B[13]);
  or or_4 (O[12], A[12], B[12]);
  or or_5 (O[11], A[11], B[11]);
  or or_6 (O[10], A[10], B[10]);
  or or_7 (O[9], A[9], B[9]);
  or or_8 (O[8], A[8], B[8]);
  or or_9 (O[7], A[7], B[7]);
  or or_10 (O[6], A[6], B[6]);
  or or_11 (O[5], A[5], B[5]);
  or or_12 (O[4], A[4], B[4]);
  or or_13 (O[3], A[3], B[3]);
  or or_14 (O[2], A[2], B[2]);
  or or_15 (O[1], A[1], B[1]);
  or or_16 (O[0], A[0], B[0]);
endmodule

module L_16_bit_XOR (
  input  [15:0] A,
  input  [15:0] B,
  output [15:0] O
);

  xor xor_1 (O[15], A[15], B[15]);
  xor xor_2 (O[14], A[14], B[14]);
  xor xor_3 (O[13], A[13], B[13]);
  xor xor_4 (O[12], A[12], B[12]);
  xor xor_5 (O[11], A[11], B[11]);
  xor xor_6 (O[10], A[10], B[10]);
  xor xor_7 (O[9], A[9], B[9]);
  xor xor_8 (O[8], A[8], B[8]);
  xor xor_9 (O[7], A[7], B[7]);
  xor xor_10 (O[6], A[6], B[6]);
  xor xor_11 (O[5], A[5], B[5]);
  xor xor_12 (O[4], A[4], B[4]);
  xor xor_13 (O[3], A[3], B[3]);
  xor xor_14 (O[2], A[2], B[2]);
  xor xor_15 (O[1], A[1], B[1]);
  xor xor_16 (O[0], A[0], B[0]);
endmodule

module L_16_bit_XOR_LE (
  input  [15:0] A,
  input  [15:0] B,
  output E,
  output L,
  output [15:0] O
);

  wire l_large_2_equal_out, l_large_2_large_out, l_large_3_equal_out, l_large_3_large_out,
       l_large_4_equal_out, l_large_4_large_out, l_large_5_equal_out, l_large_5_large_out,
       l_large_6_equal_out, l_large_6_large_out, l_large_7_equal_out, l_large_7_large_out,
       l_large_8_equal_out, l_large_8_large_out, l_large_9_equal_out, l_large_9_large_out,
       l_large_10_equal_out, l_large_10_large_out, l_large_11_equal_out, l_large_11_large_out,
       l_large_12_equal_out, l_large_12_large_out, l_large_13_equal_out, l_large_13_large_out,
       l_large_14_equal_out, l_large_14_large_out, l_large_15_equal_out, l_large_15_large_out,
       l_large_16_equal_out, l_large_16_large_out;

  L_large l_large_1 (
    .equal_out(E), .large_out(L), .o(O[15]), .equal_in(l_large_2_equal_out), .large_in(l_large_2_large_out),
    .a(A[15]), .b(B[15]));
  L_large l_large_2 (
    .equal_out(l_large_2_equal_out), .large_out(l_large_2_large_out), .o(O[14]),
    .equal_in(l_large_3_equal_out), .large_in(l_large_3_large_out), .a(A[14]), .b(B[14]));
  L_large l_large_3 (
    .equal_out(l_large_3_equal_out), .large_out(l_large_3_large_out), .o(O[13]),
    .equal_in(l_large_4_equal_out), .large_in(l_large_4_large_out), .a(A[13]), .b(B[13]));
  L_large l_large_4 (
    .equal_out(l_large_4_equal_out), .large_out(l_large_4_large_out), .o(O[12]),
    .equal_in(l_large_5_equal_out), .large_in(l_large_5_large_out), .a(A[12]), .b(B[12]));
  L_large l_large_5 (
    .equal_out(l_large_5_equal_out), .large_out(l_large_5_large_out), .o(O[11]),
    .equal_in(l_large_6_equal_out), .large_in(l_large_6_large_out), .a(A[11]), .b(B[11]));
  L_large l_large_6 (
    .equal_out(l_large_6_equal_out), .large_out(l_large_6_large_out), .o(O[10]),
    .equal_in(l_large_7_equal_out), .large_in(l_large_7_large_out), .a(A[10]), .b(B[10]));
  L_large l_large_7 (
    .equal_out(l_large_7_equal_out), .large_out(l_large_7_large_out), .o(O[9]),
    .equal_in(l_large_8_equal_out), .large_in(l_large_8_large_out), .a(A[9]), .b(B[9]));
  L_large l_large_8 (
    .equal_out(l_large_8_equal_out), .large_out(l_large_8_large_out), .o(O[8]),
    .equal_in(l_large_9_equal_out), .large_in(l_large_9_large_out), .a(A[8]), .b(B[8]));
  L_large l_large_9 (
    .equal_out(l_large_9_equal_out), .large_out(l_large_9_large_out), .o(O[7]),
    .equal_in(l_large_10_equal_out), .large_in(l_large_10_large_out), .a(A[7]), .b(B[7]));
  L_large l_large_10 (
    .equal_out(l_large_10_equal_out), .large_out(l_large_10_large_out), .o(O[6]),
    .equal_in(l_large_11_equal_out), .large_in(l_large_11_large_out), .a(A[6]), .b(B[6]));
  L_large l_large_11 (
    .equal_out(l_large_11_equal_out), .large_out(l_large_11_large_out), .o(O[5]),
    .equal_in(l_large_12_equal_out), .large_in(l_large_12_large_out), .a(A[5]), .b(B[5]));
  L_large l_large_12 (
    .equal_out(l_large_12_equal_out), .large_out(l_large_12_large_out), .o(O[4]),
    .equal_in(l_large_13_equal_out), .large_in(l_large_13_large_out), .a(A[4]), .b(B[4]));
  L_large l_large_13 (
    .equal_out(l_large_13_equal_out), .large_out(l_large_13_large_out), .o(O[3]),
    .equal_in(l_large_14_equal_out), .large_in(l_large_14_large_out), .a(A[3]), .b(B[3]));
  L_large l_large_14 (
    .equal_out(l_large_14_equal_out), .large_out(l_large_14_large_out), .o(O[2]),
    .equal_in(l_large_15_equal_out), .large_in(l_large_15_large_out), .a(A[2]), .b(B[2]));
  L_large l_large_15 (
    .equal_out(l_large_15_equal_out), .large_out(l_large_15_large_out), .o(O[1]),
    .equal_in(l_large_16_equal_out), .large_in(l_large_16_large_out), .a(A[1]), .b(B[1]));
  L_large l_large_16 (
    .equal_out(l_large_16_equal_out), .large_out(l_large_16_large_out), .o(O[0]), .equal_in(1'b1),
    .large_in(1'b0), .a(A[0]), .b(B[0]));
endmodule

module L_16_bit_ADD (
  input  [15:0] A,
  input  [15:0] B,
  input  in_3,
  output [15:0] S,
  output C,
  output Gm,
  output Pm
);

  wire four_bit_paralled_adder_1_gm, four_bit_paralled_adder_1_pm, four_bit_paralled_adder_2_gm,
       four_bit_paralled_adder_2_pm, four_bit_paralled_adder_3_gm, four_bit_paralled_adder_3_pm,
       four_bit_paralled_adder_4_gm, four_bit_paralled_adder_4_pm, four_bit_parallel_carry_1_c1,
       four_bit_parallel_carry_1_c2, four_bit_parallel_carry_1_c3;

  // Probe on A
  // Probe on B
  four_bit_paralled_adder four_bit_paralled_adder_1 (
    .A(A[3:0]), .B(B[3:0]), .S(S[3:0]), .Pm(four_bit_paralled_adder_1_pm), .Gm(four_bit_paralled_adder_1_gm));  // open: Cin, C
  four_bit_paralled_adder four_bit_paralled_adder_2 (
    .A(A[7:4]), .B(B[7:4]), .Cin(four_bit_parallel_carry_1_c1), .S(S[7:4]),
    .Pm(four_bit_paralled_adder_2_pm), .Gm(four_bit_paralled_adder_2_gm));  // open: C
  four_bit_paralled_adder four_bit_paralled_adder_3 (
    .A(A[11:8]), .B(B[11:8]), .Cin(four_bit_parallel_carry_1_c2), .S(S[11:8]),
    .Pm(four_bit_paralled_adder_3_pm), .Gm(four_bit_paralled_adder_3_gm));  // open: C
  four_bit_paralled_adder four_bit_paralled_adder_4 (
    .A(A[15:12]), .B(B[15:12]), .Cin(four_bit_parallel_carry_1_c3), .S(S[15:12]),
    .Pm(four_bit_paralled_adder_4_pm), .Gm(four_bit_paralled_adder_4_gm));  // open: C
  // Probe on S
  four_bit_parallel_carry four_bit_parallel_carry_1 (
    .G0(four_bit_paralled_adder_1_gm), .P0(four_bit_paralled_adder_1_pm), .G1(four_bit_paralled_adder_2_gm),
    .P1(four_bit_paralled_adder_2_pm), .G2(four_bit_paralled_adder_3_gm), .P2(four_bit_paralled_adder_3_pm),
    .G3(four_bit_paralled_adder_4_gm), .P3(four_bit_paralled_adder_4_pm), .Cin(in_3),
    .C1(four_bit_parallel_carry_1_c1), .C2(four_bit_parallel_carry_1_c2), .C3(four_bit_parallel_carry_1_c3),
    .C4(C), .Gm(Gm), .Pm(Pm));
endmodule

module L_16_bit_SUB (
  input  [15:0] in_1,
  input  [15:0] in_2,
  input  in_3,
  output [15:0] S,
  output C
);

  wire [15:0] xor_1_out;

  // Probe on in_1
  // Probe on in_2
  xor xor_1 (xor_1_out[0], in_2[0], in_3);
  xor xor_2 (xor_1_out[1], in_2[1], in_3);
  xor xor_3 (xor_1_out[2], in_2[2], in_3);
  xor xor_4 (xor_1_out[3], in_2[3], in_3);
  xor xor_5 (xor_1_out[4], in_2[4], in_3);
  xor xor_6 (xor_1_out[5], in_2[5], in_3);
  xor xor_7 (xor_1_out[6], in_2[6], in_3);
  xor xor_8 (xor_1_out[7], in_2[7], in_3);
  xor xor_9 (xor_1_out[8], in_2[8], in_3);
  xor xor_10 (xor_1_out[9], in_2[9], in_3);
  xor xor_11 (xor_1_out[10], in_2[10], in_3);
  xor xor_12 (xor_1_out[11], in_2[11], in_3);
  xor xor_13 (xor_1_out[12], in_2[12], in_3);
  xor xor_14 (xor_1_out[13], in_2[13], in_3);
  xor xor_15 (xor_1_out[14], in_2[14], in_3);
  xor xor_16 (xor_1_out[15], in_2[15], in_3);
  L_16_bit_ADD l_16_bit_add_1 (.A(in_1), .B(xor_1_out), .in_3(in_3), .S(S), .C(C));  // open: Gm, Pm
  // Probe on S
endmodule

module L_16_bit_SHL (
  input  shift_in,
  input  [15:0] in_2,
  output [15:0] out_3,
  output shift_out
);

  wire [14:0] reg_16_bit_1_o;

  REG_16_Bit reg_16_bit_1 (.I(in_2), .S(1'b1), .E(1'b1), .O({shift_out, reg_16_bit_1_o}));  // open: OP
  REG_16_Bit reg_16_bit_2 (.I({reg_16_bit_1_o, shift_in}), .S(1'b1), .E(1'b1), .O(out_3));  // open: OP
endmodule

module L_16_bit_SHR (
  input  [15:0] in_1,
  input  shift_in,
  output shift_out,
  output [15:0] out_4
);

  wire [15:1] reg_16_bit_1_o;

  REG_16_Bit reg_16_bit_1 (.I(in_1), .S(1'b1), .E(1'b1), .O({reg_16_bit_1_o, shift_out}));  // open: OP
  REG_16_Bit reg_16_bit_2 (.I({shift_in, reg_16_bit_1_o}), .S(1'b1), .E(1'b1), .O(out_4));  // open: OP
endmodule

module L_large (
  input  equal_in,
  input  large_in,
  input  a,
  input  b,
  output o,
  output equal_out,
  output large_out
);

  wire and_2_out, not_1_out;

  xor xor_1 (o, a, b);
  not not_1 (not_1_out, o);
  and and_1 (equal_out, not_1_out, equal_in);
  and and_2 (and_2_out, a, equal_in, o);
  or or_1 (large_out, and_2_out, large_in);
endmodule

module four_bit_paralled_adder (
  input  [3:0] A,
  input  [3:0] B,
  input  Cin,
  output [3:0] S,
  output Pm,
  output Gm,
  output C
);

  wire and_1_out, and_2_out, and_3_out, and_4_out, four_bit_parallel_carry_1_c1,
       four_bit_parallel_carry_1_c2, four_bit_parallel_carry_1_c3, or_1_out, or_2_out, or_3_out, or_4_out;

  and and_1 (and_1_out, A[0], B[0]);
  and and_2 (and_2_out, A[1], B[1]);
  and and_3 (and_3_out, A[2], B[2]);
  and and_4 (and_4_out, A[3], B[3]);
  or or_1 (or_1_out, A[0], B[0]);
  or or_2 (or_2_out, A[1], B[1]);
  or or_3 (or_3_out, A[2], B[2]);
  or or_4 (or_4_out, A[3], B[3]);
  four_bit_parallel_carry four_bit_parallel_carry_1 (
    .G0(and_1_out), .P0(or_1_out), .G1(and_2_out), .P1(or_2_out), .G2(and_3_out), .P2(or_3_out),
    .G3(and_4_out), .P3(or_4_out), .Cin(Cin), .C1(four_bit_parallel_carry_1_c1),
    .C2(four_bit_parallel_carry_1_c2), .C3(four_bit_parallel_carry_1_c3), .C4(C), .Gm(Gm), .Pm(Pm));
  full_adder full_adder_1 (.A(B[0]), .B(A[0]), .So(S[0]));  // open: C, Co
  full_adder full_adder_2 (.C(four_bit_parallel_carry_1_c1), .A(B[1]), .B(A[1]), .So(S[1]));  // open: Co
  full_adder full_adder_3 (.C(four_bit_parallel_carry_1_c2), .A(B[2]), .B(A[2]), .So(S[2]));  // open: Co
  full_adder full_adder_4 (.C(B[3]), .A(four_bit_parallel_carry_1_c3), .B(A[3]), .So(S[3]));  // open: Co
endmodule

module four_bit_parallel_adder_test (
  input  in_1
);

  wire and_1_out, clock_1_out, comparator_1_gt, undriven;
  wire [3:0] counter_1_q, counter_1_q_2, four_bit_paralled_adder_1_s;
  wire [4:4] four_bit_paralled_adder_1_c;

  Counter counter_1 (.Q({counter_1_q_2, counter_1_q}), .clk(and_1_out), .clr(in_1));  // open: load, D, count, carry, up
  // Probe on {counter_1_q_2, counter_1_q}
  Comparator comparator_1 (.a({8{1'b1}}), .b({counter_1_q_2, counter_1_q}), .gt(comparator_1_gt));  // open: eq, lt
  Clock clock_1 (.out(clock_1_out));
  and and_1 (and_1_out, comparator_1_gt, clock_1_out);
  four_bit_paralled_adder four_bit_paralled_adder_1 (
    .A(counter_1_q_2), .B(counter_1_q), .S(four_bit_paralled_adder_1_s), .C(four_bit_paralled_adder_1_c[4]));  // open: Cin, Pm, Gm
  RAM #(.dataWidth(5)) ram_1 (
    .addr({counter_1_q_2, counter_1_q}), .we(1'b1), .oe(undriven), .clk(and_1_out),
    .din({four_bit_paralled_adder_1_c[4], four_bit_paralled_adder_1_s}));  // open: dout
  // Probe on {four_bit_paralled_adder_1_c[4], four_bit_paralled_adder_1_s}
  // Probe on {four_bit_paralled_adder_1_c[4], four_bit_paralled_adder_1_s}
endmodule

module four_bit_parallel_carry (
  input  G0,
  input  P0,
  input  G1,
  input  P1,
  input  G2,
  input  P2,
  input  G3,
  input  P3,
  input  Cin,
  output C1,
  output C2,
  output C3,
  output C4,
  output Gm,
  output Pm
);

  wire and_1_out, and_2_out, and_3_out, and_4_out, and_5_out, and_6_out, and_7_out, and_8_out, and_9_out,
       and_10_out, and_11_out, and_12_out, and_13_out;

  and and_1 (and_1_out, P0, Cin);
  and and_2 (and_2_out, P1, G0);
  and and_3 (and_3_out, P1, P0, Cin);
  and and_4 (and_4_out, P2, G1);
  and and_5 (and_5_out, P2, P1, G0);
  and and_6 (and_6_out, P2, P1, P0, Cin);
  and and_7 (and_7_out, P3, G2);
  and and_8 (and_8_out, P3, P2, G1);
  and and_9 (and_9_out, P3, P2, P1, G0);
  and and_10 (and_10_out, P3, P2, P1, P0, Cin);
  and and_11 (and_11_out, P3, G2);
  and and_12 (and_12_out, P3, P2, G1);
  and and_13 (and_13_out, P3, P2, P1, G0);
  and and_14 (Pm, P3, P2, P1, P0);
  or or_1 (C1, G0, and_1_out);
  or or_2 (C2, G1, and_2_out, and_3_out);
  or or_3 (C3, G2, and_4_out, and_5_out, and_6_out);
  or or_4 (C4, G3, and_7_out, and_8_out, and_9_out, and_10_out);
  or or_5 (Gm, G3, and_11_out, and_12_out, and_13_out);
endmodule

module four_bit_adder (
  input  [3:0] A,
  input  [3:0] B,
  output [3:0] Si,
  output Ci
);

  wire full_adder_1_co, full_adder_2_co, full_adder_3_co;

  // Probe on A
  // Probe on B
  full_adder full_adder_1 (.A(A[0]), .B(B[0]), .So(Si[0]), .Co(full_adder_1_co));  // open: C
  full_adder full_adder_2 (.C(full_adder_1_co), .A(A[1]), .B(B[1]), .So(Si[1]), .Co(full_adder_2_co));
  full_adder full_adder_3 (.C(full_adder_2_co), .A(A[2]), .B(B[2]), .So(Si[2]), .Co(full_adder_3_co));
  full_adder full_adder_4 (.C(full_adder_3_co), .A(A[3]), .B(B[3]), .So(Si[3]), .Co(Ci));
endmodule

module full_adder (
  input  C,
  input  A,
  input  B,
  output So,
  output Co
);

  wire and_1_out, and_2_out, xor_1_out;

  xor xor_1 (xor_1_out, A, B);
  and and_1 (and_1_out, A, B);
  and and_2 (and_2_out, C, xor_1_out);
  xor xor_2 (So, C, xor_1_out);
  or or_1 (Co, and_2_out, and_1_out);
endmodule
