// Logisim project decoder_.circ as structural Verilog: 2 circuits, main circuit decoder_4_16
module decoder_3_8 (
  input  [2:0] in_1,
  output D0,
  output D1,
  output D2,
  output D3,
  output D4,
  output D5,
  output D6,
  output D7
);

  wire not_1_out, not_2_out, not_3_out;

  not not_1 (not_1_out, in_1[0]);
  not not_2 (not_2_out, in_1[1]);
  not not_3 (not_3_out, in_1[2]);
  and and_1 (D0, not_1_out, not_2_out, not_3_out);
  and and_2 (D1, in_1[0], not_2_out, not_3_out);
  and and_3 (D2, not_1_out, in_1[1], not_3_out);
  and and_4 (D3, in_1[0], in_1[1], not_3_out);
  and and_5 (D4, not_1_out, not_2_out, in_1[2]);
  and and_6 (D5, in_1[0], not_2_out, in_1[2]);
  and and_7 (D6, not_1_out, in_1[1], in_1[2]);
  and and_8 (D7, in_1[0], in_1[1], in_1[2]);
endmodule

module decoder_4_16 (
  input  [3:0] in_1,
  output D0,
  output D1,
  output D2,
  output D3,
  output D4,
  output D5,
  output D6,
  output D7,
  output D8,
  output D9,
  output D10,
  output D11,
  output D12,
  output D13,
  output D14,
  output D15
);

  wire not_1_out, not_2_out, not_3_out, not_4_out;

  not not_1 (not_1_out, in_1[0]);
  not not_2 (not_2_out, in_1[1]);
  not not_3 (not_3_out, in_1[2]);
  not not_4 (not_4_out, in_1[3]);
  and and_1 (D0, not_1_out, not_2_out, not_3_out, not_4_out);
  and and_2 (D1, in_1[0], not_2_out, not_3_out, not_4_out);
  and and_3 (D2, not_1_out, in_1[1], not_3_out, not_4_out);
  and and_4 (D3, in_1[0], in_1[1], not_3_out, not_4_out);
  and and_5 (D4, not_1_out, not_2_out, in_1[2], not_4_out);
  and and_6 (D5, in_1[0], not_2_out, in_1[2], not_4_out);
  and and_7 (D6, not_1_out, in_1[1], in_1[2], not_4_out);
  and and_8 (D7, in_1[0], in_1[1], in_1[2], not_4_out);
  and and_9 (D8, not_1_out, not_2_out, not_3_out, in_1[3]);
  and and_10 (D9, in_1[0], not_2_out, not_3_out, in_1[3]);
  and and_11 (D10, not_1_out, in_1[1], not_3_out, in_1[3]);
  and and_12 (D11, in_1[0], in_1[1], not_3_out, in_1[3]);
  and and_13 (D12, not_1_out, not_2_out, in_1[2], in_1[3]);
  and and_14 (D13, in_1[0], not_2_out, in_1[2], in_1[3]);
  and and_15 (D14, not_1_out, in_1[1], in_1[2], in_1[3]);
  and and_16 (D15, in_1[0], in_1[1], in_1[2], in_1[3]);
endmodule
