// Logisim project mem.circ as structural Verilog: 11 circuits, main circuit REG_16_Bit
module RAM_256 (
  input  SE,
  input  [7:0] Address,
  input  [15:0] I,
  input  RESET,
  input  S,
  input  E,
  output [15:0] O
);

  wire decoder_4_16_1_p3, decoder_4_16_1_p4, decoder_4_16_1_p5, decoder_4_16_1_p6, decoder_4_16_1_p7,
       decoder_4_16_1_p8, decoder_4_16_2_p2, decoder_4_16_2_p3, decoder_4_16_2_p4, decoder_4_16_2_p5,
       decoder_4_16_2_p6, decoder_4_16_2_p7, decoder_4_16_2_p8, decoder_4_16_2_p9, decoder_4_16_2_p10,
       decoder_4_16_2_p11, decoder_4_16_2_p12, decoder_4_16_2_p13, decoder_4_16_2_p14, decoder_4_16_2_p15,
       decoder_4_16_2_p16, decoder_4_16_2_p17;
  wire [7:0] mem_8_bit_1_o;
  wire [15:0] reg_16_bit_byte_1_o, reg_16_bit_byte_1_op, reg_16_bit_byte_2_op, reg_16_bit_byte_3_op,
       reg_16_bit_byte_4_op, reg_16_bit_byte_5_op, reg_16_bit_byte_6_op, reg_16_bit_byte_7_op,
       reg_16_bit_byte_8_op, reg_16_bit_byte_9_op, reg_16_bit_byte_10_op, reg_16_bit_byte_11_op,
       reg_16_bit_byte_12_op, reg_16_bit_byte_13_op, reg_16_bit_byte_14_op, reg_16_bit_byte_15_op,
       reg_16_bit_byte_16_op, reg_16_bit_byte_17_op, reg_16_bit_byte_18_op, reg_16_bit_byte_19_op,
       reg_16_bit_byte_20_op, reg_16_bit_byte_21_op, reg_16_bit_byte_22_op, reg_16_bit_byte_23_op,
       reg_16_bit_byte_24_op, reg_16_bit_byte_25_op, reg_16_bit_byte_26_op, reg_16_bit_byte_27_op,
       reg_16_bit_byte_28_op, reg_16_bit_byte_29_op, reg_16_bit_byte_30_op;

  MEM_8_Bit mem_8_bit_1 (.I(Address), .S(SE), .O(mem_8_bit_1_o));
  assign O = E ? reg_16_bit_byte_1_o : 16'bz;  // Controlled_Buffer controlled_buffer_1
  // decoder_4_16 decoder_4_16_1: pin names not known; wires that end beside it: mem_8_bit_1_o[3:0], mem_8_bit_1_o[7:4], decoder_4_16_1_p3, decoder_4_16_1_p4, decoder_4_16_1_p5, decoder_4_16_1_p6, decoder_4_16_1_p7, decoder_4_16_1_p8
  // decoder_4_16 decoder_4_16_2: pin names not known; wires that end beside it: mem_8_bit_1_o[7:4], decoder_4_16_2_p2, decoder_4_16_2_p3, decoder_4_16_2_p4, decoder_4_16_2_p5, decoder_4_16_2_p6, decoder_4_16_2_p7, decoder_4_16_2_p8, decoder_4_16_2_p9, decoder_4_16_2_p10, decoder_4_16_2_p11, decoder_4_16_2_p12, decoder_4_16_2_p13, decoder_4_16_2_p14, decoder_4_16_2_p15, decoder_4_16_2_p16, decoder_4_16_2_p17
  // Probe on reg_16_bit_byte_1_op
  REG_16_Bit_BYTE reg_16_bit_byte_1 (
    .OP(reg_16_bit_byte_1_op), .O(reg_16_bit_byte_1_o), .H(decoder_4_16_2_p2), .V(decoder_4_16_1_p3), .S(S),
    .E(E), .RESET(RESET), .I(I));
  // Probe on reg_16_bit_byte_2_op
  REG_16_Bit_BYTE reg_16_bit_byte_2 (
    .OP(reg_16_bit_byte_2_op), .O(reg_16_bit_byte_1_o), .H(decoder_4_16_2_p3), .V(decoder_4_16_1_p3), .S(S),
    .E(E), .RESET(RESET), .I(I));
  // Probe on reg_16_bit_byte_3_op
  REG_16_Bit_BYTE reg_16_bit_byte_3 (
    .OP(reg_16_bit_byte_3_op), .O(reg_16_bit_byte_1_o), .H(decoder_4_16_2_p4), .V(decoder_4_16_1_p3), .S(S),
    .E(E), .RESET(RESET), .I(I));
  // Probe on reg_16_bit_byte_4_op
  REG_16_Bit_BYTE reg_16_bit_byte_4 (
    .OP(reg_16_bit_byte_4_op), .O(reg_16_bit_byte_1_o), .H(decoder_4_16_2_p5), .V(decoder_4_16_1_p3), .S(S),
    .E(E), .RESET(RESET), .I(I));
  // Probe on reg_16_bit_byte_5_op
  REG_16_Bit_BYTE reg_16_bit_byte_5 (
    .OP(reg_16_bit_byte_5_op), .O(reg_16_bit_byte_1_o), .H(decoder_4_16_2_p6), .V(decoder_4_16_1_p3), .S(S),
    .E(E), .RESET(RESET), .I(I));
  // Probe on reg_16_bit_byte_6_op
  REG_16_Bit_BYTE reg_16_bit_byte_6 (
    .OP(reg_16_bit_byte_6_op), .O(reg_16_bit_byte_1_o), .H(decoder_4_16_2_p2), .V(decoder_4_16_1_p4), .S(S),
    .E(E), .RESET(RESET), .I(I));
  // Probe on reg_16_bit_byte_7_op
  REG_16_Bit_BYTE reg_16_bit_byte_7 (
    .OP(reg_16_bit_byte_7_op), .O(reg_16_bit_byte_1_o), .H(decoder_4_16_2_p3), .V(decoder_4_16_1_p4), .S(S),
    .E(E), .RESET(RESET), .I(I));
  // Probe on reg_16_bit_byte_8_op
  REG_16_Bit_BYTE reg_16_bit_byte_8 (
    .OP(reg_16_bit_byte_8_op), .O(reg_16_bit_byte_1_o), .H(decoder_4_16_2_p4), .V(decoder_4_16_1_p4), .S(S),
    .E(E), .RESET(RESET), .I(I));
  // Probe on reg_16_bit_byte_9_op
  REG_16_Bit_BYTE reg_16_bit_byte_9 (
    .OP(reg_16_bit_byte_9_op), .O(reg_16_bit_byte_1_o), .H(decoder_4_16_2_p5), .V(decoder_4_16_1_p4), .S(S),
    .E(E), .RESET(RESET), .I(I));
  // Probe on reg_16_bit_byte_10_op
  REG_16_Bit_BYTE reg_16_bit_byte_10 (
    .OP(reg_16_bit_byte_10_op), .O(reg_16_bit_byte_1_o), .H(decoder_4_16_2_p6), .V(decoder_4_16_1_p4), .S(S),
    .E(E), .RESET(RESET), .I(I));
  // Probe on reg_16_bit_byte_11_op
  REG_16_Bit_BYTE reg_16_bit_byte_11 (
    .OP(reg_16_bit_byte_11_op), .O(reg_16_bit_byte_1_o), .H(decoder_4_16_2_p2), .V(decoder_4_16_1_p5), .S(S),
    .E(E), .RESET(RESET), .I(I));
  // Probe on reg_16_bit_byte_12_op
  REG_16_Bit_BYTE reg_16_bit_byte_12 (
    .OP(reg_16_bit_byte_12_op), .O(reg_16_bit_byte_1_o), .H(decoder_4_16_2_p3), .V(decoder_4_16_1_p5), .S(S),
    .E(E), .RESET(RESET), .I(I));
  // Probe on reg_16_bit_byte_13_op
  REG_16_Bit_BYTE reg_16_bit_byte_13 (
    .OP(reg_16_bit_byte_13_op), .O(reg_16_bit_byte_1_o), .H(decoder_4_16_2_p4), .V(decoder_4_16_1_p5), .S(S),
    .E(E), .RESET(RESET), .I(I));
  // Probe on reg_16_bit_byte_14_op
  REG_16_Bit_BYTE reg_16_bit_byte_14 (
    .OP(reg_16_bit_byte_14_op), .O(reg_16_bit_byte_1_o), .H(decoder_4_16_2_p5), .V(decoder_4_16_1_p5), .S(S),
    .E(E), .RESET(RESET), .I(I));
  // Probe on reg_16_bit_byte_15_op
  REG_16_Bit_BYTE reg_16_bit_byte_15 (
    .OP(reg_16_bit_byte_15_op), .O(reg_16_bit_byte_1_o), .H(decoder_4_16_2_p6), .V(decoder_4_16_1_p5), .S(S),
    .E(E), .RESET(RESET), .I(I));
  // Probe on reg_16_bit_byte_16_op
  REG_16_Bit_BYTE reg_16_bit_byte_16 (
    .OP(reg_16_bit_byte_16_op), .O(reg_16_bit_byte_1_o), .H(decoder_4_16_2_p2), .V(decoder_4_16_1_p6), .S(S),
    .E(E), .RESET(RESET), .I(I));
  // Probe on reg_16_bit_byte_17_op
  REG_16_Bit_BYTE reg_16_bit_byte_17 (
    .OP(reg_16_bit_byte_17_op), .O(reg_16_bit_byte_1_o), .H(decoder_4_16_2_p3), .V(decoder_4_16_1_p6), .S(S),
    .E(E), .RESET(RESET), .I(I));
  // Probe on reg_16_bit_byte_18_op
  REG_16_Bit_BYTE reg_16_bit_byte_18 (
    .OP(reg_16_bit_byte_18_op), .O(reg_16_bit_byte_1_o), .H(decoder_4_16_2_p4), .V(decoder_4_16_1_p6), .S(S),
    .E(E), .RESET(RESET), .I(I));
  // Probe on reg_16_bit_byte_19_op
  REG_16_Bit_BYTE reg_16_bit_byte_19 (
    .OP(reg_16_bit_byte_19_op), .O(reg_16_bit_byte_1_o), .H(decoder_4_16_2_p5), .V(decoder_4_16_1_p6), .S(S),
    .E(E), .RESET(RESET), .I(I));
  // Probe on reg_16_bit_byte_20_op
  REG_16_Bit_BYTE reg_16_bit_byte_20 (
    .OP(reg_16_bit_byte_20_op), .O(reg_16_bit_byte_1_o), .H(decoder_4_16_2_p6), .V(decoder_4_16_1_p6), .S(S),
    .E(E), .RESET(RESET), .I(I));
  // Probe on reg_16_bit_byte_21_op
  REG_16_Bit_BYTE reg_16_bit_byte_21 (
    .OP(reg_16_bit_byte_21_op), .O(reg_16_bit_byte_1_o), .H(decoder_4_16_2_p2), .V(decoder_4_16_1_p7), .S(S),
    .E(E), .RESET(RESET), .I(I));
  // Probe on reg_16_bit_byte_22_op
  REG_16_Bit_BYTE reg_16_bit_byte_22 (
    .OP(reg_16_bit_byte_22_op), .O(reg_16_bit_byte_1_o), .H(decoder_4_16_2_p3), .V(decoder_4_16_1_p7), .S(S),
    .E(E), .RESET(RESET), .I(I));
  // Probe on reg_16_bit_byte_23_op
  REG_16_Bit_BYTE reg_16_bit_byte_23 (
    .OP(reg_16_bit_byte_23_op), .O(reg_16_bit_byte_1_o), .H(decoder_4_16_2_p4), .V(decoder_4_16_1_p7), .S(S),
    .E(E), .RESET(RESET), .I(I));
  // Probe on reg_16_bit_byte_24_op
  REG_16_Bit_BYTE reg_16_bit_byte_24 (
    .OP(reg_16_bit_byte_24_op), .O(reg_16_bit_byte_1_o), .H(decoder_4_16_2_p5), .V(decoder_4_16_1_p7), .S(S),
    .E(E), .RESET(RESET), .I(I));
  // Probe on reg_16_bit_byte_25_op
  REG_16_Bit_BYTE reg_16_bit_byte_25 (
    .OP(reg_16_bit_byte_25_op), .O(reg_16_bit_byte_1_o), .H(decoder_4_16_2_p6), .V(decoder_4_16_1_p7), .S(S),
    .E(E), .RESET(RESET), .I(I));
  // Probe on reg_16_bit_byte_26_op
  REG_16_Bit_BYTE reg_16_bit_byte_26 (
    .OP(reg_16_bit_byte_26_op), .O(reg_16_bit_byte_1_o), .H(decoder_4_16_2_p2), .V(decoder_4_16_1_p8), .S(S),
    .E(E), .RESET(RESET), .I(I));
  // Probe on reg_16_bit_byte_27_op
  REG_16_Bit_BYTE reg_16_bit_byte_27 (
    .OP(reg_16_bit_byte_27_op), .O(reg_16_bit_byte_1_o), .H(decoder_4_16_2_p3), .V(decoder_4_16_1_p8), .S(S),
    .E(E), .RESET(RESET), .I(I));
  // Probe on reg_16_bit_byte_28_op
  REG_16_Bit_BYTE reg_16_bit_byte_28 (
    .OP(reg_16_bit_byte_28_op), .O(reg_16_bit_byte_1_o), .H(decoder_4_16_2_p4), .V(decoder_4_16_1_p8), .S(S),
    .E(E), .RESET(RESET), .I(I));
  // Probe on reg_16_bit_byte_29_op
  REG_16_Bit_BYTE reg_16_bit_byte_29 (
    .OP(reg_16_bit_byte_29_op), .O(reg_16_bit_byte_1_o), .H(decoder_4_16_2_p5), .V(decoder_4_16_1_p8), .S(S),
    .E(E), .RESET(RESET), .I(I));
  // Probe on reg_16_bit_byte_30_op
  REG_16_Bit_BYTE reg_16_bit_byte_30 (
    .OP(reg_16_bit_byte_30_op), .O(reg_16_bit_byte_1_o), .H(decoder_4_16_2_p6), .V(decoder_4_16_1_p8), .S(S),
    .E(E), .RESET(RESET), .I(I));
endmodule

module REG_16_Bit_BYTE (
  input  [15:0] I,
  input  H,
  input  RESET,
  input  V,
  input  S,
  input  E,
  output [15:0] O,
  output [15:0] OP
);

  wire and_1_out, and_2_out, and_3_out, or_1_out;
  wire [15:0] reg_16_bit_1_o;

  and and_1 (and_1_out, H, V);
  and and_2 (and_2_out, and_1_out, S);
  and and_3 (and_3_out, and_1_out, E);
  or or_1 (or_1_out, RESET, and_2_out);
  assign O = and_3_out ? reg_16_bit_1_o : 16'bz;  // Controlled_Buffer controlled_buffer_1
  REG_16_Bit reg_16_bit_1 (.I(I), .S(or_1_out), .E(and_3_out), .OP(OP), .O(reg_16_bit_1_o));
endmodule

module REG_16_Bit (
  input  [15:0] I,
  input  S,
  input  E,
  output [15:0] OP,
  output [15:0] O
);

  wire [15:0] enable_16_bit_1_o;

  MEM_16_Bit mem_16_bit_1 (.I(I), .S(S), .O(OP));
  ENABLE_16_Bit enable_16_bit_1 (.I(OP), .E(E), .O(enable_16_bit_1_o));
  assign O = E ? enable_16_bit_1_o : 16'bz;  // Controlled_Buffer controlled_buffer_1
endmodule

module ENABLE_16_Bit (
  input  [15:0] I,
  input  E,
  output [15:0] O
);

  wire and_1_out, and_2_out, and_3_out, and_4_out, and_5_out, and_6_out, and_7_out, and_8_out, and_9_out,
       and_10_out, and_11_out, and_12_out, and_13_out, and_14_out, and_15_out, and_16_out;

  and and_1 (and_1_out, I[0], E);
  and and_2 (and_2_out, I[1], E);
  and and_3 (and_3_out, I[2], E);
  and and_4 (and_4_out, I[3], E);
  and and_5 (and_5_out, I[4], E);
  and and_6 (and_6_out, I[5], E);
  and and_7 (and_7_out, I[6], E);
  and and_8 (and_8_out, I[7], E);
  and and_9 (and_9_out, I[8], E);
  and and_10 (and_10_out, I[9], E);
  and and_11 (and_11_out, I[10], E);
  and and_12 (and_12_out, I[11], E);
  and and_13 (and_13_out, I[12], E);
  and and_14 (and_14_out, I[13], E);
  and and_15 (and_15_out, I[14], E);
  and and_16 (and_16_out, I[15], E);
  assign O[0] = E ? and_1_out : 1'bz;  // Controlled_Buffer controlled_buffer_1
  assign O[1] = E ? and_2_out : 1'bz;  // Controlled_Buffer controlled_buffer_2
  assign O[2] = E ? and_3_out : 1'bz;  // Controlled_Buffer controlled_buffer_3
  assign O[3] = E ? and_4_out : 1'bz;  // Controlled_Buffer controlled_buffer_4
  assign O[4] = E ? and_5_out : 1'bz;  // Controlled_Buffer controlled_buffer_5
  assign O[5] = E ? and_6_out : 1'bz;  // Controlled_Buffer controlled_buffer_6
  assign O[6] = E ? and_7_out : 1'bz;  // Controlled_Buffer controlled_buffer_7
  assign O[7] = E ? and_8_out : 1'bz;  // Controlled_Buffer controlled_buffer_8
  assign O[8] = E ? and_9_out : 1'bz;  // Controlled_Buffer controlled_buffer_9
  assign O[9] = E ? and_10_out : 1'bz;  // Controlled_Buffer controlled_buffer_10
  assign O[10] = E ? and_11_out : 1'bz;  // Controlled_Buffer controlled_buffer_11
  assign O[11] = E ? and_12_out : 1'bz;  // Controlled_Buffer controlled_buffer_12
  assign O[12] = E ? and_13_out : 1'bz;  // Controlled_Buffer controlled_buffer_13
  assign O[13] = E ? and_14_out : 1'bz;  // Controlled_Buffer controlled_buffer_14
  assign O[14] = E ? and_15_out : 1'bz;  // Controlled_Buffer controlled_buffer_15
  assign O[15] = E ? and_16_out : 1'bz;  // Controlled_Buffer controlled_buffer_16
endmodule

module MEM_16_Bit (
  input  [15:0] I,
  input  S,
  output [15:0] O
);

  MEM_1_Bit mem_1_bit_1 (.Q(O[0]), .I(I[0]), .S(S));
  MEM_1_Bit mem_1_bit_2 (.Q(O[1]), .I(I[1]), .S(S));
  MEM_1_Bit mem_1_bit_3 (.Q(O[2]), .I(I[2]), .S(S));
  MEM_1_Bit mem_1_bit_4 (.Q(O[3]), .I(I[3]), .S(S));
  MEM_1_Bit mem_1_bit_5 (.Q(O[4]), .I(I[4]), .S(S));
  MEM_1_Bit mem_1_bit_6 (.Q(O[5]), .I(I[5]), .S(S));
  MEM_1_Bit mem_1_bit_7 (.Q(O[6]), .I(I[6]), .S(S));
  MEM_1_Bit mem_1_bit_8 (.Q(O[7]), .I(I[7]), .S(S));
  MEM_1_Bit mem_1_bit_9 (.Q(O[8]), .I(I[8]), .S(S));
  MEM_1_Bit mem_1_bit_10 (.Q(O[9]), .I(I[9]), .S(S));
  MEM_1_Bit mem_1_bit_11 (.Q(O[10]), .I(I[10]), .S(S));
  MEM_1_Bit mem_1_bit_12 (.Q(O[11]), .I(I[11]), .S(S));
  MEM_1_Bit mem_1_bit_13 (.Q(O[12]), .I(I[12]), .S(S));
  MEM_1_Bit mem_1_bit_14 (.Q(O[13]), .I(I[13]), .S(S));
  MEM_1_Bit mem_1_bit_15 (.Q(O[14]), .I(I[14]), .S(S));
  MEM_1_Bit mem_1_bit_16 (.Q(O[15]), .I(I[15]), .S(S));
endmodule

module MEM_8_Bit (
  input  [7:0] I,
  input  S,
  output [7:0] O
);

  MEM_1_Bit mem_1_bit_1 (.Q(O[0]), .I(I[0]), .S(S));
  MEM_1_Bit mem_1_bit_2 (.Q(O[1]), .I(I[1]), .S(S));
  MEM_1_Bit mem_1_bit_3 (.Q(O[2]), .I(I[2]), .S(S));
  MEM_1_Bit mem_1_bit_4 (.Q(O[3]), .I(I[3]), .S(S));
  MEM_1_Bit mem_1_bit_5 (.Q(O[4]), .I(I[4]), .S(S));
  MEM_1_Bit mem_1_bit_6 (.Q(O[5]), .I(I[5]), .S(S));
  MEM_1_Bit mem_1_bit_7 (.Q(O[6]), .I(I[6]), .S(S));
  MEM_1_Bit mem_1_bit_8 (.Q(O[7]), .I(I[7]), .S(S));
endmodule

module MEM_1_Bit (
  input  I,
  input  S,
  output Q
);

  wire A_out, B_out, D_out;

  nand A (A_out, I, S);
  nand B (B_out, A_out, S);
  nand C (Q, A_out, D_out);
  nand D (D_out, Q, B_out);
endmodule

module RS_Flip_Flop (
  input  S,
  input  R,
  output Q,
  output NQ
);

  nand nand_1 (Q, S, NQ);
  nand nand_2 (NQ, Q, R);
endmodule

module RS_Flip_Flop_Clock (
  input  S,
  input  E,
  input  R,
  output Q,
  output NQ
);

  wire nand_1_out, nand_2_out;

  nand nand_1 (nand_1_out, S, E);
  nand nand_2 (nand_2_out, E, R);
  nand nand_3 (Q, nand_1_out, NQ);
  nand nand_4 (NQ, Q, nand_2_out);
endmodule

module D_Flip_Flop_CLock (
  input  S,
  input  E,
  output Q,
  output NQ
);

  wire nand_1_out, nand_2_out, not_1_out;

  not not_1 (not_1_out, S);
  nand nand_1 (nand_1_out, S, E);
  nand nand_2 (nand_2_out, E, not_1_out);
  nand nand_3 (Q, nand_1_out, NQ);
  nand nand_4 (NQ, Q, nand_2_out);
endmodule

module D_Flip_Flop_Clock_2 (
  input  in_1,
  input  in_2,
  output out_3,
  output out_4
);

  wire nand_1_out, nand_2_out;

  nand nand_1 (nand_1_out, in_1, in_2);
  nand nand_2 (nand_2_out, nand_1_out, in_2);
  nand nand_3 (out_3, nand_1_out, out_4);
  nand nand_4 (out_4, out_3, nand_2_out);
endmodule
